# Fritzing sketch carrito wifisocket (saved by Fritzing 0.9.3b)

parts:
  U1 = NodeMCU V1.0
  BAT1 = BC9VPC [package=bc9vpc]
  S1 = H-Bridge with L298N
  M1 = DC Motor
  M2 = DC Motor
  M3 = DC Motor
  M4 = DC Motor

nets:
  N1: U1.D0, S1.IN4
  N2: U1.D1, S1.IN3
  N3: U1.D2, S1.IN2
  N4: U1.D3, S1.IN1
  GND: U1.GND, BAT1.V-, S1.GND
  N5: BAT1.V+, S1.12V
  N6: S1.ENA, S1.ENA-5V
  N7: S1.ENB, S1.ENB-5V
  N8: S1.M1-01, M2.pin_2, M3.pin_2
  N9: S1.M1-02, M2.pin_1, M3.pin_1
  N10: S1.M2-01, M1.pin_2, M4.pin_2
  N11: S1.M2-02, M1.pin_1, M4.pin_1

custom parts:
  NodeMCU V1.0: ESP8266 based NodeMCU V1.0
  H-Bridge with L298N: h-bridge
